# Fritzing sketch DHT11 (saved by Fritzing 0.9.3b)
breadboards: 1

parts:
  Bauteil1 = Arduino Uno (Rev3)
  RHT1 = Humidity and Temperature Sensor RHT03
  Bauteil2 = Arduino Ethernet Shield (Rev3)

nets:
  N1: Bauteil1.D8, RHT1.Vcc, Bauteil2.D8
  GND: Bauteil1.GND, RHT1.GND_2, Bauteil2.GND
  5V: Bauteil1.5V, RHT1.Data-signal, Bauteil2.5V
